// Logisim project Counter.circ as structural Verilog: 2 circuits, main circuit main
module main (
  input  CLK,
  input  R,
  input  P,
  output [3:0] \export ,
  output Pexport,
  output C
);

  wire multiplexer_1_out;
  wire [3:0] adder_1_out;

  Register #(.width(4)) register_1 (.D(adder_1_out), .clk(CLK), .Q(\export ), .clr(multiplexer_1_out));  // open: en
  Multiplexer #(.enable("false")) multiplexer_1 (.in0(C), .in1(R), .out(multiplexer_1_out), .sel(R));
  Adder #(.width(4)) adder_1 (.a(\export ), .b(4'b0001), .out(adder_1_out));  // open: cin, cout
  Comparator #(.mode("unsigned"), .width(4)) comparator_1 (.a(\export ), .b(4'b1001), .gt(C));  // open: eq, lt

  assign Pexport = P;
endmodule

module a (
  input  Stop,
  input  Mux,
  input  MUX1
);

  wire Add_out, C, M2, M3, main_1_c, main_2_c, main_3_c, multiplexer_1_out, multiplexer_2_out, PCR,
       Reset_out, Start_out;
  wire [3:0] main_1_export, main_2_export, main_3_export, main_4_export, multiplexer_4_out,
       multiplexer_5_out, multiplexer_6_out, multiplexer_7_out;
  wire [7:0] adder_1_out, multiplexer_8_out, register_1_q, subtractor_1_out;
  wire [15:0] ram_1_dout;

  Button Write (.out(M3));
  Button OutputM2 (.out(M2));
  Button Add (.out(Add_out));
  Button u_PCR (.out(PCR));
  Clock Start (.out(Start_out));
  Button Reset (.out(Reset_out));
  Multiplexer #(.enable("false")) multiplexer_1 (.in0(M3), .in1(M2), .out(multiplexer_1_out), .sel(M2));
  Multiplexer #(.enable("false")) multiplexer_2 (.in0(Start_out), .in1(1'b0), .out(multiplexer_2_out), .sel(Stop));
  Multiplexer #(.enable("false")) multiplexer_3 (.in0(multiplexer_1_out), .in1(Add_out), .out(C), .sel(Add_out));
  main main_1 (.CLK(multiplexer_2_out), .R(Reset_out), .\export (main_1_export), .C(main_1_c));  // open: P, Pexport
  main main_2 (.CLK(main_1_c), .R(Reset_out), .\export (main_2_export), .C(main_2_c));  // open: P, Pexport
  main main_3 (.CLK(main_2_c), .R(Reset_out), .\export (main_3_export), .C(main_3_c));  // open: P, Pexport
  main main_4 (.CLK(main_3_c), .R(Reset_out), .\export (main_4_export));  // open: P, Pexport, C
  Hex_Digit_Display hex_digit_display_1 (.value(multiplexer_7_out));  // open: dp
  Multiplexer #(.enable("false"), .width(4)) multiplexer_4 (
    .in0(main_1_export), .in1(ram_1_dout[3:0]), .out(multiplexer_4_out), .sel(MUX1));
  Multiplexer #(.enable("false"), .width(4)) multiplexer_5 (
    .in0(main_2_export), .in1(ram_1_dout[7:4]), .out(multiplexer_5_out), .sel(MUX1));
  Multiplexer #(.enable("false"), .width(4)) multiplexer_6 (
    .in0(main_3_export), .in1(ram_1_dout[11:8]), .out(multiplexer_6_out), .sel(MUX1));
  Multiplexer #(.enable("false"), .width(4)) multiplexer_7 (
    .in0(main_4_export), .in1(ram_1_dout[15:12]), .out(multiplexer_7_out), .sel(MUX1));
  Hex_Digit_Display hex_digit_display_2 (.value(multiplexer_6_out));  // open: dp
  Hex_Digit_Display hex_digit_display_3 (.value(multiplexer_5_out));  // open: dp
  Register register_1 (.D(multiplexer_8_out), .clk(C), .Q(register_1_q), .clr(PCR));  // open: en
  Hex_Digit_Display hex_digit_display_4 (.value(multiplexer_4_out));  // open: dp
  RAM #(.dataWidth(16)) ram_1 (
    .addr(register_1_q), .we(M3), .oe(M2), .clk(C),
    .din({multiplexer_7_out, multiplexer_6_out, multiplexer_5_out, multiplexer_4_out}), .dout(ram_1_dout));
  Adder adder_1 (.a(register_1_q), .b(8'h1), .out(adder_1_out));  // open: cin, cout
  Multiplexer #(.enable("false"), .width(8)) multiplexer_8 (
    .in0(adder_1_out), .in1(subtractor_1_out), .out(multiplexer_8_out), .sel(Mux));
  Subtractor subtractor_1 (.a(register_1_q), .b(8'h1), .out(subtractor_1_out));  // open: bin, bout

  // Other names for the same wires on the sheet: Sub = Mux
endmodule
